# Fritzing sketch circuit_diagram (saved by Fritzing 0.7.12b)
breadboards: 1

parts:
  Arduino1 = Arduino
  IC1 = H-Bridge [package=THT]
  R1 = Rotary Potentiometer (Small) [maximum_resistance=100kΩ]
  VCC1 = Battery block 9V
  M1 = DC Motor
  M2 = DC Motor

nets:
  N1: Arduino1.D10, IC1.3_4EN
  N2: Arduino1.D9, IC1.1_2EN
  N3: Arduino1.D6, IC1.4A
  N4: Arduino1.D5, IC1.3A
  N5: Arduino1.D4, IC1.1A
  N6: Arduino1.D3, IC1.2A
  GND: Arduino1.GND, IC1.GND1, IC1.GND2, VCC1.-
  N7: Arduino1.A0, R1.wiper
  N8: IC1.1Y, M1.pin_2
  N9: IC1.2Y, M1.pin_1
  N10: IC1.VCC2, VCC1.+
  N11: IC1.3Y, M2.pin_1
  GND3: IC1.GND3, IC1.GND4, R1.leg1
  N12: IC1.4Y, M2.pin_2
  N13: IC1.VCC1, R1.leg2
